# Fritzing sketch mysimon (saved by Fritzing 0.9.10b)
breadboards: 1

parts:
  Componente1 = Arduino Uno (Rev3)
  J1 = Piezo Speaker
  S1 = Pushbutton [package="[THT]"]
  S2 = Pushbutton [package="[THT]"]
  S3 = Pushbutton [package="[THT]"]
  S4 = Pushbutton [package="[THT]"]
  U2 = WS2812 RGB LED strip [mn=50 mpn=10]

nets:
  N1: Componente1.D8, S3.Pin_3, S3.Pin_4
  N2: Componente1.D9_PWM, S4.Pin_3, S4.Pin_4
  N3: Componente1.D11_PWM/MOSI, J1.pin2
  N4: Componente1.D12/MISO, U2.DIN
  N5: Componente1.D6_PWM, S1.Pin_3, S1.Pin_4
  N6: Componente1.D7, S2.Pin_3, S2.Pin_4
  N7: J1.pin1, U2.GND
  N8: S1.Pin_1, S1.Pin_2, S2.Pin_1, S2.Pin_2, S3.Pin_1, S3.Pin_2, S4.Pin_1, S4.Pin_2, U2.VCC

custom parts:
  WS2812 RGB LED strip: WS2812 strip
